// Logisim project ALU.circ as structural Verilog
module OneBitFullAdder (
  input  a_n,
  input  b_n,
  input  c_n,
  output s_n,
  output c_next
);

  wire and_1_out, and_2_out, and_3_out, xor_1_out;

  and and_1 (and_1_out, b_n, a_n);
  and and_2 (and_2_out, c_n, b_n);
  and and_3 (and_3_out, c_n, a_n);
  xor xor_1 (xor_1_out, a_n, b_n);
  or or_1 (c_next, and_1_out, and_2_out, and_3_out);
  xor xor_2 (s_n, xor_1_out, c_n);
endmodule

module EightBitAdder (
  input  C_n,
  input  [7:0] A,
  input  [7:0] B,
  output [7:0] S,
  output C_next
);

  wire onebitfulladder_1_c_next, onebitfulladder_2_c_next, onebitfulladder_3_c_next,
       onebitfulladder_4_c_next, onebitfulladder_5_c_next, onebitfulladder_6_c_next, onebitfulladder_7_c_next;

  OneBitFullAdder onebitfulladder_1 (.a_n(A[0]), .b_n(B[0]), .c_n(C_n), .s_n(S[0]), .c_next(onebitfulladder_1_c_next));
  OneBitFullAdder onebitfulladder_2 (
    .a_n(A[1]), .b_n(B[1]), .c_n(onebitfulladder_1_c_next), .s_n(S[1]), .c_next(onebitfulladder_2_c_next));
  OneBitFullAdder onebitfulladder_3 (
    .a_n(A[2]), .b_n(B[2]), .c_n(onebitfulladder_2_c_next), .s_n(S[2]), .c_next(onebitfulladder_3_c_next));
  OneBitFullAdder onebitfulladder_4 (
    .a_n(A[3]), .b_n(B[3]), .c_n(onebitfulladder_3_c_next), .s_n(S[3]), .c_next(onebitfulladder_4_c_next));
  OneBitFullAdder onebitfulladder_5 (
    .a_n(A[4]), .b_n(B[4]), .c_n(onebitfulladder_4_c_next), .s_n(S[4]), .c_next(onebitfulladder_5_c_next));
  OneBitFullAdder onebitfulladder_6 (
    .a_n(A[5]), .b_n(B[5]), .c_n(onebitfulladder_5_c_next), .s_n(S[5]), .c_next(onebitfulladder_6_c_next));
  OneBitFullAdder onebitfulladder_7 (
    .a_n(A[6]), .b_n(B[6]), .c_n(onebitfulladder_6_c_next), .s_n(S[6]), .c_next(onebitfulladder_7_c_next));
  OneBitFullAdder onebitfulladder_8 (
    .a_n(A[7]), .b_n(B[7]), .c_n(onebitfulladder_7_c_next), .s_n(S[7]), .c_next(C_next));
endmodule

module ALU (
  input  [2:0] OP,
  input  [7:0] A,
  input  [7:0] B,
  output [7:0] S,
  output [3:0] Status
);

  wire and_3_out, and_4_out, not_3_out, not_4_out, not_5_out, Sub_Is_Selected;
  wire [7:0] A_and_B, A_LS_B, A_or_B, A_RS_B, A_xor_B, Add_Sub_S, Arithmetic_A_RS_B, B_ALU,
       multiplexer_3_out, not_1_out, Not_A;
  wire [15:8] shifter_3_out;

  and and_1 (Sub_Is_Selected, OP[0], ~OP[1], ~OP[2]);  // AND_Gate
  Multiplexer #(.select(3), .width(8)) multiplexer_1 (
    .in0(Add_Sub_S), .in1(Add_Sub_S), .in2(A_and_B), .in3(A_or_B), .in4(Arithmetic_A_RS_B), .in5(A_xor_B),
    .in6(A_LS_B), .in7(A_RS_B), .out(S), .sel(OP));
  assign not_1_out = ~B;  // NOT_Gate not_1, 8 bits wide
  Multiplexer #(.width(8)) multiplexer_2 (.in0(B), .in1(not_1_out), .out(B_ALU), .sel(Sub_Is_Selected));
  assign A_and_B = A & B;  // AND_Gate and_2, 8 bits wide
  assign Not_A = ~A;  // NOT_Gate not_2, 8 bits wide
  Shifter shifter_1 (.in(A), .\dist (B[2:0]), .out(A_LS_B));
  EightBitAdder eightbitadder_1 (.C_n(Sub_Is_Selected), .A(A), .B(B_ALU), .S(Add_Sub_S), .C_next(Status[1]));
  assign A_or_B = A | B;  // OR_Gate or_1, 8 bits wide
  assign A_xor_B = A ^ B;  // XOR_Gate xor_1, 8 bits wide
  Shifter #(.shift("lr")) shifter_2 (.in(A), .\dist (B[2:0]), .out(A_RS_B));
  nor nor_1 (Status[2], S[0], S[1], S[2], S[3], S[4], S[5], S[6], S[7]);
  not not_3 (not_3_out, S[7]);
  not not_4 (not_4_out, A[7]);
  not not_5 (not_5_out, B_ALU[7]);
  Multiplexer #(.width(8)) multiplexer_3 (.in0({8{1'b0}}), .in1({8{1'b1}}), .out(multiplexer_3_out), .sel(A[7]));
  and and_3 (and_3_out, A[7], B_ALU[7], not_3_out);
  and and_4 (and_4_out, not_5_out, not_4_out, S[7]);
  or or_2 (Status[0], and_3_out, and_4_out);
  Shifter #(.shift("lr"), .width(16)) shifter_3 (
    .in({multiplexer_3_out, A}), .\dist ({1'b0, B[2:0]}), .out({shifter_3_out, Arithmetic_A_RS_B}));

  assign Status[3] = S[7];

  // Other names for the same wires on the sheet: A_MSB = A[7]; V = Status[0]; C = Status[1]; Z = Status[2]; N = S[7]

  // Notes on the sheet:
  //   MSB of A
  //   Output Control
  //   Check if the current operation is substraction
  //   Not A
  //   And
  //   A << B
  //   Adder/Subtractor
  //   Or
  //   A xor B
  //   A >> B
  //   Status
endmodule

module MyMultiplier (
  input  [7:0] B
);

  wire clk, load_clk, shift_clk;
  wire [7:0] A;

  Clock clock_1 (.out(clk));
  D_Flip_Flop d_ff_1 (.D(load_clk), .clk(clk), .Q(shift_clk), .Qn(load_clk));  // open: preset, reset
  // Shift_Register shift_register_1: pin names not known; wires that end beside it: A
  ALU alu_1 (.OP(3'b000), .B(B));  // open: A, S, Status

  // Notes on the sheet:
  //   Clock Module
  //   Select Addition
endmodule
